# Fritzing sketch esp8266-proj (saved by Fritzing 0.9.3b)
breadboards: 1

parts:
  U1 = ESP8266 NodeMCU LoLin module
  Part1 = Max Power IR LED Kit
  J1 = Piezo Speaker
  IC1 = Voltage Regulator [package=78xxl]
  VCC1 = Battery block 9V
  C1 = Capacitor Polarized [package=cpol-radial-10uf-25v]
  C2 = Capacitor Polarized [package=cpol-radial-10uf-25v]

nets:
  N1: U1.D1, Part1.CONTROL
  N2: U1.D2, J1.pin2
  GND: U1.GND, Part1.GND, J1.pin1
  N3: U1.Vin, IC1.OUT, C2.+
  3V3: U1.3V3, Part1.VCC
  N4: IC1.GND, VCC1.-, C1.-
  N5: IC1.IN, VCC1.+, C1.+, C2.-

notes:
  Driver Drowsiness Detection System
  Main System
  Power Supply
  Snehasree S

custom parts:
  ESP8266 NodeMCU LoLin module: ESP8266 based NodeMCU
